# Fritzing sketch gameboy (saved by Fritzing 1.0.1rc)
circuit board: 8.46667cm x 5.64444cm
breadboards: 1

parts:
  A2 = Raspberry Pi 3 Model A+
  Power_Button = Pushbutton [package="[THT]"]
  B_Button = Pushbutton [package="[THT]"]
  Start_Button = Pushbutton [package="[THT]"]
  Select_Button = Pushbutton [package="[THT]"]
  Right_Arrow = Pushbutton [package="[THT]"]
  Up_Arrow = Pushbutton [package="[THT]"]
  Down_Arrow = Pushbutton [package="[THT]"]
  Left_Arrow = Pushbutton [package="[THT]"]
  A_Button = Pushbutton [package="[THT]"]

nets:
  N1: A2.Pin_1, A2.Pin_38, Power_Button.Pin_1, Power_Button.Pin_2, B_Button.Pin_1, B_Button.Pin_2, Start_Button.Pin_1, Start_Button.Pin_2, Select_Button.Pin_1, Select_Button.Pin_2, Right_Arrow.Pin_3, Right_Arrow.Pin_4, Up_Arrow.Pin_1, Up_Arrow.Pin_2, Down_Arrow.Pin_1, Down_Arrow.Pin_2, Left_Arrow.Pin_1, Left_Arrow.Pin_2, A_Button.Pin_3, A_Button.Pin_4
  N2: A2.Pin_2, Select_Button.Pin_3, Select_Button.Pin_4
  N3: A2.Pin_3, Start_Button.Pin_3, Start_Button.Pin_4
  N4: A2.Pin_4, B_Button.Pin_3, B_Button.Pin_4
  N5: A2.Pin_5, A_Button.Pin_1, A_Button.Pin_2
  N6: A2.Pin_18, Power_Button.Pin_3, Power_Button.Pin_4
  N7: A2.Pin_21, Left_Arrow.Pin_3, Left_Arrow.Pin_4
  N8: A2.Pin_22, Up_Arrow.Pin_3, Up_Arrow.Pin_4
  N9: A2.Pin_23, Down_Arrow.Pin_3, Down_Arrow.Pin_4
  N10: A2.Pin_25, Right_Arrow.Pin_1, Right_Arrow.Pin_2

custom parts:
  Raspberry Pi 3 Model A+: The Raspberry Pi 3 Model A+ is the latest product in the Raspberry Pi 3 range. Like the Raspberry Pi 3 Model B+, it boasts a 64-bit quad core processor running at 1.4 GHz, dual-band 2.4 GHz and 5 GHz wireless LAN, and Bluetooth 4.2/BLE.
